// Logisim project DDCA.circ as structural Verilog: 3 circuits, main circuit main
module main (
  input  Cin_Mode,
  input  A3,
  input  A2,
  input  A1,
  input  A0,
  input  B3,
  input  B2,
  input  B1,
  input  B0,
  output S3,
  output S2,
  output S1,
  output S0,
  output Cout
);

  _4_bit_adder_subtracter u_4_bit_adder_subtracter_1 (
    .Cin(Cin_Mode), .A0(A0), .A1(A1), .A2(A2), .A3(A3), .B0(B0), .B1(B1), .B2(B2), .B3(B3), .S0(S0), .S1(S1),
    .S2(S2), .S3(S3), .Cout(Cout));
endmodule

module Full_adder (
  input  Cin,
  input  A,
  input  B,
  output SO,
  output Cout
);

  wire and_1_out, and_2_out, xor_1_out;

  xor xor_1 (xor_1_out, Cin, A);
  and and_1 (and_1_out, Cin, A);
  and and_2 (and_2_out, xor_1_out, B);
  xor xor_2 (SO, xor_1_out, B);
  or or_1 (Cout, and_1_out, and_2_out);
endmodule

module _4_bit_adder_subtracter (
  input  Cin,
  input  A0,
  input  A1,
  input  A2,
  input  A3,
  input  B0,
  input  B1,
  input  B2,
  input  B3,
  output S0,
  output S1,
  output S2,
  output S3,
  output Cout
);

  wire full_adder_1_cout, full_adder_2_cout, full_adder_3_cout, xor_1_out, xor_2_out, xor_3_out, xor_4_out;

  xor xor_1 (xor_1_out, Cin, B0);
  xor xor_2 (xor_2_out, Cin, B1);
  xor xor_3 (xor_3_out, Cin, B2);
  xor xor_4 (xor_4_out, Cin, B3);
  Full_adder full_adder_1 (.Cin(Cin), .A(A0), .B(xor_1_out), .SO(S0), .Cout(full_adder_1_cout));
  Full_adder full_adder_2 (.Cin(full_adder_1_cout), .A(A1), .B(xor_2_out), .SO(S1), .Cout(full_adder_2_cout));
  Full_adder full_adder_3 (.Cin(full_adder_2_cout), .A(A2), .B(xor_3_out), .SO(S2), .Cout(full_adder_3_cout));
  Full_adder full_adder_4 (.Cin(full_adder_3_cout), .A(A3), .B(xor_4_out), .SO(S3), .Cout(Cout));
endmodule
